// Logisim project riscv32-circuit.circ as structural Verilog: 8 circuits, main circuit RISCV32
module RISCV32 (
);

  wire and_1_out, and_2_out, and_3_out, and_5_out, and_6_out, Clk_out, comparator_black_box_1_p4,
       comparator_black_box_1_p5, control_1_alusrc, control_1_branch, control_1_memread, control_1_memtoreg,
       control_1_memwrite, control_1_regwrite, nor_1_out, not_1_out, ram_1_p3, ram_1_p6, ram_1_p7,
       registerfile_1_p3;
  wire [1:0] alu_1_p4;
  wire [2:0] control_1_aluop;
  wire [3:0] alucontrol_1_aluopout, ram_1_p4;
  wire [4:0] instructionmemory_1_instr11_7, instructionmemory_1_instr19_15, instructionmemory_1_instr24_20,
       multiplexer_6_out;
  wire [6:0] instructionmemory_1_instr6_0;
  wire [19:0] alu_1_p4_2;
  wire [29:0] register_1_q_2;
  wire [31:0] bit_extender_1_out, dataramout_1_p3, immgen_1_imm, instructionmemory_1_instr31_0,
       multiplexer_1_out, multiplexer_2_out, multiplexer_3_out, multiplexer_4_out, multiplexer_5_out,
       multiplexer_7_out, ram_1_p2, register_1_q, registerfile_1_p7, registerfile_1_p8;
  wire [31:5] multiplexer_6_out_2;
  wire [31:22] alu_1_p4_3;

  Clock Clk (.out(Clk_out));
  Multiplexer #(.width(32)) multiplexer_1 (
    .in0(register_1_q), .in1({alu_1_p4_3, alu_1_p4_2, alu_1_p4}), .out(multiplexer_1_out), .sel(and_3_out));
  Register #(.width(32)) register_1 (
    .D(multiplexer_1_out), .clk(Clk_out), .Q({register_1_q_2, register_1_q[1:0]}));  // open: en, clr
  // Incrementer #(.width(30)) incrementer_1: pin names not known; wires that end beside it: register_1_q_2, register_1_q[31:2]
  Multiplexer #(.width(32)) multiplexer_2 (
    .in0(multiplexer_3_out), .in1(immgen_1_imm), .out(multiplexer_2_out), .sel(and_2_out));
  InstructionMemory instructionmemory_1 (
    .PC({register_1_q_2, register_1_q[1:0]}), .Instr6_0(instructionmemory_1_instr6_0),
    .Instr19_15(instructionmemory_1_instr19_15), .Instr24_20(instructionmemory_1_instr24_20),
    .Instr11_7(instructionmemory_1_instr11_7), .Instr31_0(instructionmemory_1_instr31_0));
  Multiplexer #(.width(32)) multiplexer_3 (
    .in0(multiplexer_7_out), .in1(bit_extender_1_out), .out(multiplexer_3_out), .sel(and_1_out));
  and and_1 (and_1_out, instructionmemory_1_instr31_0[0], instructionmemory_1_instr31_0[1], ~instructionmemory_1_instr31_0[2], ~instructionmemory_1_instr31_0[3], instructionmemory_1_instr31_0[4], instructionmemory_1_instr31_0[5], ~instructionmemory_1_instr31_0[6], ~instructionmemory_1_instr31_0[12], instructionmemory_1_instr31_0[13], ~instructionmemory_1_instr31_0[14]);  // AND_Gate
  Control control_1 (
    .Opcode(instructionmemory_1_instr6_0), .Branch(control_1_branch), .MemRead(control_1_memread),
    .MemtoReg(control_1_memtoreg), .ALUOp(control_1_aluop), .MemWrite(control_1_memwrite),
    .ALUSrc(control_1_alusrc), .RegWrite(control_1_regwrite));
  // RegisterFile registerfile_1: pin names not known; wires that end beside it: multiplexer_2_out, Clk_out, registerfile_1_p3, instructionmemory_1_instr11_7, instructionmemory_1_instr19_15, instructionmemory_1_instr24_20, registerfile_1_p7, registerfile_1_p8
  ImmGen immgen_1 (.Instr31_0(instructionmemory_1_instr31_0), .Imm(immgen_1_imm));
  ALUControl alucontrol_1 (
    .Func({instructionmemory_1_instr31_0[30], instructionmemory_1_instr31_0[14:12]}),
    .ALUOpIn(control_1_aluop), .ALUOpOut(alucontrol_1_aluopout));
  Multiplexer #(.width(32)) multiplexer_4 (
    .in0(registerfile_1_p7), .in1({register_1_q_2, register_1_q[1:0]}), .out(multiplexer_4_out),
    .sel(control_1_branch));
  Multiplexer #(.width(32)) multiplexer_5 (
    .in0(registerfile_1_p8), .in1(immgen_1_imm), .out(multiplexer_5_out), .sel(control_1_alusrc));
  // ALU alu_1: pin names not known; wires that end beside it: multiplexer_4_out, multiplexer_5_out, alucontrol_1_aluopout, {alu_1_p4_3, alu_1_p4_2, alu_1_p4}
  // Comparator_Black_Box comparator_black_box_1: pin names not known; wires that end beside it: registerfile_1_p7, registerfile_1_p8, instructionmemory_1_instr31_0[13], comparator_black_box_1_p4, comparator_black_box_1_p5
  Multiplexer #(.width(32)) multiplexer_6 (
    .in0(registerfile_1_p8), .in1(immgen_1_imm), .out({multiplexer_6_out_2, multiplexer_6_out}),
    .sel(control_1_aluop[2]));
  and and_2 (and_2_out, ~control_1_aluop[0], ~control_1_aluop[1], control_1_aluop[2]);  // AND_Gate
  and and_3 (and_3_out, control_1_branch, comparator_black_box_1_p4);
  assign bit_extender_1_out = {{31{1'b0}}, comparator_black_box_1_p5};  // Bit_Extender bit_extender_1
  // RAM ram_1: pin names not known; wires that end beside it: alu_1_p4_2, ram_1_p2, ram_1_p3, ram_1_p4, Clk_out, ram_1_p6, ram_1_p7
  Multiplexer #(.width(32)) multiplexer_7 (
    .in0({alu_1_p4_3, alu_1_p4_2, alu_1_p4}), .in1(dataramout_1_p3), .out(multiplexer_7_out),
    .sel(control_1_memtoreg));
  SelectCS selectcs_1 (.CSBit(alu_1_p4), .Op_13(instructionmemory_1_instr31_0[13]), .CSOut(ram_1_p4));
  DataRAMIn dataramin_1 (.Data(registerfile_1_p8), .CS(ram_1_p4), .ModifiedData(ram_1_p2));
  // DataRAMOut dataramout_1: pin names not known; wires that end beside it: ram_1_p7, ram_1_p4, dataramout_1_p3
  and and_4 (registerfile_1_p3, not_1_out, control_1_regwrite);
  nor nor_1 (nor_1_out, alu_1_p4_3[22], alu_1_p4_3[23], alu_1_p4_3[24], alu_1_p4_3[25], alu_1_p4_3[26], alu_1_p4_3[28], alu_1_p4_3[29], alu_1_p4_3[30], alu_1_p4_3[31], alu_1_p4_3[27]);
  and and_5 (and_5_out, ~instructionmemory_1_instr31_0[0], ~instructionmemory_1_instr31_0[1], ~instructionmemory_1_instr31_0[2], ~instructionmemory_1_instr31_0[3], ~instructionmemory_1_instr31_0[4], instructionmemory_1_instr31_0[5], instructionmemory_1_instr31_0[6]);  // AND_Gate
  and and_6 (and_6_out, and_5_out, ~nor_1_out);  // AND_Gate
  not not_1 (not_1_out, and_6_out);
  and and_7 (ram_1_p6, nor_1_out, control_1_memread);
  and and_8 (ram_1_p3, nor_1_out, control_1_memwrite);

  // Notes on the sheet:
  //   PC + imm
  //   The 32-Bit RISC-V Processor
  //   PC + 4
  //   SLT Operation Detection
  //   Load Operation Overflow Detection
endmodule

module InstructionMemory (
  input  [31:0] PC,
  output [6:0] Instr6_0,
  output [4:0] Instr19_15,
  output [4:0] Instr24_20,
  output [4:0] Instr11_7,
  output [31:0] Instr31_0
);

  // RISC_VProgramROM risc_vprogramrom_1: pin names not known; wires that end beside it: PC, {Instr31_0[31:25], Instr24_20, Instr19_15, Instr31_0[14:12], Instr11_7, Instr6_0}

  assign {Instr31_0[24:15], Instr31_0[11:0]} = {Instr24_20, Instr19_15, Instr11_7, Instr6_0};

  // Notes on the sheet:
  //   contents of risc_vprogramrom_1 (hex, n*v repeats v):
  //   ## cycles = 1 # I can also write comments like this ## start[1] = 100 ## start[2] = 250 ## start[3]
  //   = 0 ## start[4] = 10 ## start[5] = 5 ## expect[1] = 250 ## expect[2] = 250 ## expect[3] = 11 ##
  //   expect[4] = 10 ## expect[5] = 10 add x1, x3, x2 addi x3, x4, 1 addi x5, x5, 5
endmodule

module Control (
  input  [6:0] Opcode,
  output Branch,
  output MemRead,
  output MemtoReg,
  output [2:0] ALUOp,
  output MemWrite,
  output ALUSrc,
  output RegWrite
);

  wire and_3_out, and_4_out, not_1_out, not_2_out;

  not not_1 (not_1_out, Opcode[6]);
  not not_2 (not_2_out, Opcode[5]);
  not not_3 (MemtoReg, Opcode[4]);
  and and_1 (MemRead, not_2_out, MemtoReg);
  or or_1 (ALUOp[2], Opcode[2], Opcode[6]);
  and and_2 (ALUOp[1], not_1_out, MemtoReg);
  and and_3 (and_3_out, not_2_out, Opcode[4]);
  and and_4 (and_4_out, Opcode[5], MemtoReg);
  and and_5 (MemWrite, not_1_out, Opcode[5], MemtoReg);
  or or_2 (ALUSrc, not_2_out, MemtoReg, Opcode[2]);
  or or_3 (RegWrite, not_2_out, Opcode[4]);
  or or_4 (ALUOp[0], and_3_out, and_4_out);

  assign Branch = Opcode[6];
endmodule

module ImmGen (
  input  [31:0] Instr31_0,
  output [31:0] Imm
);

  wire [0:0] not_1_out;
  wire [11:0] bit_extender_2_out;
  wire [31:0] bit_extender_1_out, bit_extender_3_out, bit_extender_4_out, multiplexer_2_out;

  assign bit_extender_1_out = {{20{Instr31_0[31]}}, Instr31_0[31:20]};  // Bit_Extender bit_extender_1
  assign bit_extender_2_out = {{11{1'b0}}, Instr31_0[6]};  // Bit_Extender bit_extender_2
  Multiplexer #(.select(2), .width(32)) multiplexer_1 (
    .in0(bit_extender_1_out), .in1(bit_extender_1_out), .in2(multiplexer_2_out),
    .in3({Instr31_0[31:12], bit_extender_2_out}), .out(Imm), .sel(Instr31_0[5:4]));
  not not_1 (not_1_out[0], Instr31_0[6]);
  assign bit_extender_3_out = {{20{Instr31_0[30]}}, {Instr31_0[30:25], Instr31_0[11:7], not_1_out[0]}};  // Bit_Extender bit_extender_3
  assign bit_extender_4_out = {{20{Instr31_0[31]}}, {Instr31_0[31:25], Instr31_0[11:7]}};  // Bit_Extender bit_extender_4
  Multiplexer #(.width(32)) multiplexer_2 (
    .in0(bit_extender_4_out), .in1(bit_extender_3_out), .out(multiplexer_2_out), .sel(Instr31_0[6]));
endmodule

module ALUControl (
  input  [3:0] Func,
  input  [2:0] ALUOpIn,
  output [3:0] ALUOpOut
);

  wire and_1_out, and_2_out, and_3_out, and_4_out, and_5_out, not_1_out, not_2_out, not_3_out;

  not not_1 (not_1_out, ALUOpIn[2]);
  not not_2 (not_2_out, ALUOpIn[1]);
  not not_3 (not_3_out, ALUOpIn[0]);
  and and_1 (and_1_out, Func[1], not_1_out, not_2_out);
  and and_2 (and_2_out, Func[2], ALUOpIn[0]);
  and and_3 (and_3_out, Func[2], not_1_out);
  and and_4 (and_4_out, Func[3], not_1_out, not_2_out, not_3_out);
  and and_5 (and_5_out, ALUOpIn[2], not_3_out);
  or or_1 (ALUOpOut[3], and_1_out, and_2_out);
  or or_2 (ALUOpOut[2], and_3_out, and_4_out);
  or or_3 (ALUOpOut[1], and_5_out, Func[0]);
  xnor xnor_1 (ALUOpOut[0], ALUOpIn[0], ALUOpIn[0]);
endmodule

module SelectCS (
  input  [1:0] CSBit,
  input  Op_13,
  output [3:0] CSOut
);

  wire and_1_out, and_2_out, and_3_out, and_4_out, not_1_out, not_2_out;

  not not_1 (not_1_out, CSBit[1]);
  not not_2 (not_2_out, CSBit[0]);
  or or_1 (CSOut[3], Op_13, and_1_out);
  and and_1 (and_1_out, CSBit[1], CSBit[0]);
  or or_2 (CSOut[2], Op_13, and_2_out);
  and and_2 (and_2_out, CSBit[1], not_2_out);
  or or_3 (CSOut[1], Op_13, and_3_out);
  and and_3 (and_3_out, not_1_out, CSBit[0]);
  and and_4 (and_4_out, not_1_out, not_2_out);
  or or_4 (CSOut[0], and_4_out, Op_13);
endmodule

module DataRAMIn (
  input  [31:0] Data,
  input  [3:0] CS,
  output [31:0] ModifiedData
);

  wire and_1_out;

  and and_1 (and_1_out, CS[0], CS[1], CS[2], CS[3]);
  Multiplexer #(.width(32)) multiplexer_1 (
    .in0({Data[7:0], Data[7:0], Data[7:0], Data[7:0]}), .in1(Data), .out(ModifiedData), .sel(and_1_out));
endmodule

module DataRAMOut (
  input  [31:0] Data,
  input  [3:0] CS,
  output [31:0] ModifiedData
);

  wire and_1_out, not_1_out, not_2_out, not_3_out;
  wire [1:0] and_3_out;
  wire [7:0] multiplexer_1_out;
  wire [31:0] bit_extender_1_out;

  Multiplexer #(.select(2), .width(8)) multiplexer_1 (
    .in0(Data[7:0]), .in1(Data[15:8]), .in2(Data[23:16]), .in3(Data[31:24]), .out(multiplexer_1_out),
    .sel(and_3_out));
  and and_1 (and_1_out, CS[0], CS[1], CS[2], CS[3]);
  Multiplexer #(.width(32)) multiplexer_2 (.in0(bit_extender_1_out), .in1(Data), .out(ModifiedData), .sel(and_1_out));
  assign bit_extender_1_out = {{24{1'b0}}, multiplexer_1_out};  // Bit_Extender bit_extender_1
  not not_1 (not_1_out, CS[2]);
  not not_2 (not_2_out, CS[1]);
  not not_3 (not_3_out, CS[0]);
  and and_2 (and_3_out[1], not_2_out, not_3_out);
  and and_3 (and_3_out[0], not_1_out, not_3_out);
endmodule
